# Fritzing sketch Electronics (saved by Fritzing 0.9.3b)
breadboards: 1

parts:
  Part1 = Itsy Bitsy 32u4 5V @ 16MHz [part_number="Adafruit #3677"]
  Part2 = Adafruit WINC1500 (uFL Antenna) Breakout [part_number="Adafruit #3060"]
  Part3 = TFT 1.8 inch 160x128 w microSD [part_number=358]
  2N_3906_PNP_Transistor = PNP-Transistor [package="TO92 [THT]"]
  R1 = Resistor [tolerance=±5% resistance=10 package=THT]
  R2 = Resistor [tolerance=±5% resistance=10 package=THT]  # not connected
  IR_Receiver_LED = smd LED [color="Infrared (940nm)" package="1206 [SMD]"]
  IR_Emitter_LED = LED - 5mm [color="White (8000K)" package="5 mm [THT]"]
  R3 = Resistor [tolerance=±10% resistance=1k package=THT]
  Power_Supply_3_3V = Battery

nets:
  N1: Part1.D13, Part3.TFTCS
  N2: Part1.D12, Part3.CARDCS
  N3: Part1.D11, Part3.TFTDC
  N4: Part1.D7, Part3.RESET
  N5: Part1.D1, Part2.RST
  N6: Part1.D0, Part2.CS, Part2.IRQ
  N7: Part1.MISO, Part2.MISO, Part3.MISO
  N8: Part1.MOSI, Part2.MOSI, Part3.MOSI
  N9: Part1.SCK, Part2.SCK
  N10: Part1.A1, R3.Pin_0
  N11: Part1.A0, IR_Receiver_LED.cathode
  +5V: Part2.+5V, Part2.EN, Part3.LITE, Part3.+5V, 2N_3906_PNP_Transistor.C, Power_Supply_3_3V.+
  GND: Part2.GND, Part3.GND, R1.Pin_1, IR_Receiver_LED.anode, IR_Emitter_LED.cathode
  N12: 2N_3906_PNP_Transistor.B, R3.Pin_1

custom parts:
  Itsy Bitsy 32u4 5V @ 16MHz: What's smaller than a Feather but larger than a Trinket? It's an Itsy Bitsy! Small, powerful, Arduino-compatible - this microcontroller board is perfect when you want something very compact, but still with a bunch of pins. Itsy Bitsy is only 1.4" long by 0.7" wide, but has 6 power pins, 6 analog & digital pins and 17 digital pins. It packs much of the same capability as an Arduino UNO. So it's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
  Adafruit WINC1500 (uFL Antenna) Breakout: Connect your Arduino to the Internet with this fine new FCC-certified WiFi module from Atmel. This 802.11bgn-capable WiFi module is the best new thing for networking your devices, with SSL support and rock solid performance - running our adafruit.io MQTT demo for a full weekend straight with no hiccups (it would have run longer but we had to go to work, so we unplugged it). We like these so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
  TFT 1.8 inch 160x128 w microSD: This lovely little display breakout is the best way to add a small, colorful and bright display to any project. Since the display uses 4-wire SPI to communicate and has its own pixel-addressable frame buffer, it can be used with every kind of microcontroller. Even a very small one with low memory and few pins available! The 1.8" display has 128x160 color pixels.
